# Fritzing sketch FireSystemConnections (saved by Fritzing 1.0.6)
breadboards: 1

parts:
  Mod1 = Amica NodeMCU DEVKIT 1.0
  Part1 = Arduino Uno (Rev3)
  Water_Pump = DC Motor [voltage_(max)=6V voltage_(min)=3V]
  Alarm = Piezo Speaker
  Relay = 2 channel relay module [package=THT]
  T1 = LM35 Temperature Sensor [package="TO92 [THT]"]
  J3 = Basic Servo
  12V = 4 x AAA Battery Mount [internal_resistance=0.1Ω]
  Mod2 = MQ-7 breakout
  S1 = KY-026
  C1 = Electrolytic Capacitor [capacitance=1mF voltage=16V package="100 mil [THT, electrolytic]"]

nets (from the breadboard view):
  N1: Mod1.pin1, Mod1.pin_10, Mod1.pin_26
  GND: Mod1.pin2, Mod1.pin_9, Mod1.pin_25, Mod1.pin_29, Part1.GND, Relay.pin_14, T1.GND, J3.gnd, Mod2.GND, S1.pin2, C1.-
  N2: Mod1.pin_13, Part1.A5/SCL
  N3: Mod1.pin_14, Part1.A4/SDA
  VCC: Mod1.pin_30, Part1.5V, Relay.pin_13, T1.+Vs, J3.vcc, Mod2.VCC, S1.pin3, C1.+
  N4: Part1.A0, Mod2.AO
  N5: Part1.A1, T1.Vout
  N6: Part1.D9_PWM, J3.pulse
  N7: Part1.D12/MISO, Relay.pin_15
  N8: Part1.D13/SCK, Relay.pin_16
  N9: Part1.D6_PWM, S1.pin4
  N10: Water_Pump.pin_1, Relay.pin_4
  N11: Water_Pump.pin_2, Alarm.pin1, 12V.-
  N12: Alarm.pin2, Relay.pin_1
  N13: Relay.pin_2, Relay.pin_5, 12V.+

notes:
  Arduino <-> ESP
  Switching from UART Communication to
  I2C Communication
  Before: PIN 10/11 <-> PIN D1/D2
  After: PIN A4/A5 <-> PIN D1/D2

custom parts:
  2 channel relay module: 2 channel Relay Module 5V 12V 24V High and Low Level Trigger Relay Control With Optocoupler Two Way relays DC 5 V 12 V 24 V Volt.
  MQ-7 breakout: MP-2 gas sensor
  KY-026: ky-026 flame sensor module
